// Logisim project ControllerUnity.circ as structural Verilog: 1 circuit, main circuit ControllerUnity
module ControllerUnity (
  input  [5:0] OpCode,
  output [1:0] ALUOp,
  output RegDst,
  output WriteReg,
  output ALUSrc,
  output MemToReg,
  output MemRead,
  output MemWrite,
  output Branch,
  output Bne,
  output Jump,
  output Link
);

  wire J_out, or_2_out;
  wire [0:0] Addi_out;
  wire [1:0] or_1_out;
  wire [1:1] Beq_out;

  // Probe on OpCode
  Multiplexer #(.width(2), .enable("false")) multiplexer_1 (.in0(2'b11), .in1(or_1_out), .out(ALUOp), .sel(or_2_out));
  assign or_1_out = {Bne, 1'b0} | {Beq_out[1], 1'b0} | {1'b0, MemWrite} | {1'b0, MemRead} | {1'b0, Addi_out[0]} | 2'b00;  // OR_Gate or_1, 2 bits wide
  or or_2 (or_2_out, Bne, Beq_out[1], MemWrite, MemRead, Addi_out[0], RegDst);
  and R (RegDst, ~OpCode[0], ~OpCode[1], ~OpCode[2], ~OpCode[3], ~OpCode[4], ~OpCode[5]);  // AND_Gate
  and Addi (Addi_out[0], ~OpCode[0], ~OpCode[1], ~OpCode[2], OpCode[3], ~OpCode[4], ~OpCode[5]);  // AND_Gate
  and LW (MemRead, OpCode[0], OpCode[1], ~OpCode[2], ~OpCode[3], ~OpCode[4], OpCode[5]);  // AND_Gate
  and SW (MemWrite, OpCode[0], OpCode[1], ~OpCode[2], OpCode[3], ~OpCode[4], OpCode[5]);  // AND_Gate
  and Beq (Beq_out[1], ~OpCode[0], ~OpCode[1], OpCode[2], ~OpCode[3], ~OpCode[4], ~OpCode[5]);  // AND_Gate
  and u_Bne (Bne, OpCode[0], ~OpCode[1], OpCode[2], ~OpCode[3], ~OpCode[4], ~OpCode[5]);  // AND_Gate
  and J (J_out, ~OpCode[0], OpCode[1], ~OpCode[2], ~OpCode[3], ~OpCode[4], ~OpCode[5]);  // AND_Gate
  and Jal (Link, OpCode[0], OpCode[1], ~OpCode[2], ~OpCode[3], ~OpCode[4], ~OpCode[5]);  // AND_Gate
  or or_3 (WriteReg, RegDst, Addi_out[0], MemRead, Link);
  or or_4 (ALUSrc, Addi_out[0], MemRead, MemWrite);
  or or_5 (Branch, Beq_out[1], Bne);
  or or_6 (Jump, J_out, Link);

  assign MemToReg = MemRead;
endmodule
