// Logisim project Decoder.circ as structural Verilog: 1 circuit, main circuit Decoder
module Decoder (
  input  [31:0] INST,
  output [5:0] FUNCT,
  output [4:0] SHAMT,
  output [15:0] IMM,
  output [25:0] ADDR,
  output [4:0] RD,
  output [4:0] RT,
  output [4:0] RS,
  output [5:0] Opcode
);


  assign ADDR = INST[25:0];
  assign FUNCT = INST[5:0];
  assign IMM = INST[15:0];
  assign Opcode = INST[31:26];
  assign RD = INST[15:11];
  assign RS = INST[25:21];
  assign RT = INST[20:16];
  assign SHAMT = INST[10:6];
endmodule
