// Logisim project SignalExtensor.circ as structural Verilog: 1 circuit, main circuit Extensor
module Extensor (
  input  [15:0] in_1,
  output [31:0] out_2
);


  assign out_2 = {{17{in_1[15]}}, in_1[14:0]};
endmodule
