// Logisim project ULA.circ as structural Verilog: 4 circuits, main circuit main
module main (
  input  [31:0] A,
  input  [31:0] A_2,
  input  [31:0] B,
  input  [4:0] ShAmt,
  input  [3:0] Op_ALU,
  output zero,
  output [31:0] S,
  output overflow
);

  wire and_2_out, and_3_out, comparator_1_lt, or_2_out, overflow_1_overflow;
  wire [31:0] adder_1_out, and_1_out, n1_bit_to_32_1_out_2, nor_1_out, or_1_out, shifter_1_out,
       shifter_2_out, subtractor_1_out, xor_1_out;

  // Probe on A
  // Probe on A_2
  Adder #(.width(32)) adder_1 (.a(A), .b(A_2), .out(adder_1_out));  // open: cin, cout
  Shifter #(.width(32)) shifter_1 (.in(A), .\dist (ShAmt), .out(shifter_1_out));
  Subtractor #(.width(32)) subtractor_1 (.a(A), .b(A_2), .out(subtractor_1_out));  // open: bin, bout
  Shifter #(.width(32), .shift("lr")) shifter_2 (.in(A), .\dist (ShAmt), .out(shifter_2_out));
  assign and_1_out = A & A_2;  // AND_Gate and_1, 32 bits wide
  assign or_1_out = A | A_2;  // OR_Gate or_1, 32 bits wide
  assign xor_1_out = A ^ A_2;  // XOR_Gate xor_1, 32 bits wide
  assign nor_1_out = ~(A | A_2);  // NOR_Gate nor_1, 32 bits wide
  Comparator #(.width(32)) comparator_1 (.a(A), .b(A_2), .lt(comparator_1_lt));  // open: gt, eq
  _1_bit_to_32 u_1_bit_to_32_1 (.in_1(comparator_1_lt), .out_2(n1_bit_to_32_1_out_2));
  Multiplexer #(.select(4), .width(32), .enable("false")) multiplexer_1 (
    .in0(adder_1_out), .in1(shifter_1_out), .in2(subtractor_1_out), .in3(shifter_2_out), .in4(and_1_out),
    .in5(or_1_out), .in6(xor_1_out), .in7(nor_1_out), .in8({32{1'b0}}), .in9(n1_bit_to_32_1_out_2), .out(S),
    .sel(Op_ALU));  // open: in10, in11, in12, in13, in14, in15
  overflow overflow_1 (.A(A), .B(A), .R(S), .Overflow(overflow_1_overflow));
  and and_2 (and_2_out, ~Op_ALU[3], ~Op_ALU[2], ~Op_ALU[1], ~Op_ALU[0]);  // AND_Gate
  and and_3 (and_3_out, ~Op_ALU[0], Op_ALU[1], ~Op_ALU[2], ~Op_ALU[3]);  // AND_Gate
  _32b_equals_zero u_32b_equals_zero_1 (.R(S));  // open: out_2
  or or_2 (or_2_out, and_2_out, and_3_out);
  and and_4 (overflow, overflow_1_overflow, or_2_out);
endmodule

module overflow (
  input  [31:0] A,
  input  [31:0] B,
  input  [31:0] R,
  output Overflow
);

  wire and_1_out, and_2_out, not_1_out, not_2_out, not_3_out, not_4_out;

  not not_1 (not_1_out, A[31]);
  not not_2 (not_2_out, B[31]);
  not not_3 (not_3_out, B[31]);
  not not_4 (not_4_out, R[31]);
  and and_1 (and_1_out, not_1_out, not_2_out, R[31]);
  and and_2 (and_2_out, A[31], not_3_out, not_4_out);
  or or_1 (Overflow, and_1_out, and_2_out);
endmodule

module _32b_equals_zero (
  input  [31:0] R,
  output out_2
);

  and and_1 (out_2, ~R[31], ~R[30], ~R[29], ~R[28], ~R[27], ~R[26], ~R[25], ~R[24], ~R[23], ~R[22], ~R[21], ~R[20], ~R[19], ~R[18], ~R[17], ~R[16], ~R[15], ~R[14], ~R[13], ~R[12], ~R[11], ~R[10], ~R[9], ~R[8], ~R[7], ~R[6], ~R[5], ~R[4], ~R[3], ~R[2], ~R[1], ~R[0]);  // AND_Gate
endmodule

module _1_bit_to_32 (
  input  in_1,
  output [31:0] out_2
);


  assign out_2 = {32{in_1}};
endmodule
